# Fritzing sketch Prototyp_V1 (saved by Fritzing 0.9.3b)
breadboards: 1

parts:
  Bauteil1 = Arduino Ethernet Shield (Rev3)
  hc-sr1 = hc-sr04
  hc-sr2 = hc-sr04

nets:
  N1: Bauteil1.ETH_CS, hc-sr2.Trig
  N2: Bauteil1.PWM_D11, hc-sr2.Echo
  N3: Bauteil1.SPI/D12, hc-sr1.Trig
  N4: Bauteil1.SPI/D13, hc-sr1.Echo
  VCC: hc-sr1.VCC, hc-sr2.VCC
  GND: hc-sr1.GND, hc-sr2.GND
