# Fritzing sketch Prototyp_V2 (saved by Fritzing 0.9.3b)
breadboards: 1

parts:
  Bauteil1 = Arduino Ethernet Shield (Rev3)
  hc-sr1 = hc-sr04
  hc-sr2 = hc-sr04
  hc-sr3 = hc-sr04
  hc-sr4 = hc-sr04
  hc-sr5 = hc-sr04

nets:
  N1: Bauteil1.PWM_D5, hc-sr1.Trig, hc-sr1.Echo
  VCC: hc-sr1.VCC, hc-sr2.VCC
  GND: hc-sr1.GND, hc-sr2.GND
  N2: hc-sr2.Trig, hc-sr2.Echo
  VCC_2: hc-sr3.VCC, hc-sr4.VCC, hc-sr5.VCC
  N3: hc-sr3.Trig, hc-sr3.Echo
  GND_2: hc-sr3.GND, hc-sr4.GND, hc-sr5.GND
  N4: hc-sr4.Trig, hc-sr4.Echo
  N5: hc-sr5.Trig, hc-sr5.Echo
